# Fritzing sketch mybargraph_atmega8_tqfp32 (saved by Fritzing 0.9.3b)
breadboards: 1

parts:
  C2 = Electrolytic Capacitor [capacitance=10µF voltage=35V package="0605 [SMD, electrolytic]"]
  C3 = Ceramic Capacitor [capacitance=100nF voltage=10V package="1206 [SMD, multilayer]"]
  C1 = Tantalum Capacitor [capacitance=1μF voltage=10V package="C 6032 [SMD, tantalum]"]
  U1 = Voltage Regulator - 5V [package="DPak [SMD]"]
  U$1 = MICROCONTROLLER [package=tqfp32-08]
  R1 = Resistor [tolerance=±5% resistance=100 package="2010 [SMD]"]
  JP1 = Header 1 [package=1x01_offset]
  JP2 = Header 1 [package=1x01_offset]
  D1 = LED_BARGRAPH_10 [package=led_bargaph_10]

nets:
  GND: C2.-, C3.1, C1.-, U1.GND, U$1.GND, U$1.AGND, JP2.1
  N1: C2.+, U1.input_voltage
  N2: C3.0, C1.+, U1.output_voltage, U$1.VCC, U$1.AVCC, U$1.AREF, R1.Pin_0
  N3: U$1.PD3(INT1), JP1.1
  N4: U$1.PD4(XCK_T0), D1.B_C
  N5: U$1.PB6(XTAL1_TOSC1), D1.C_C
  N6: U$1.PB7(XTAL2_TOSC2), D1.D_C
  N7: U$1.PD5(T1), D1.E_C
  N8: U$1.PD6(AIN0), D1.F_C
  N9: U$1.PD7(AIN1), D1.G_C
  N10: U$1.PB0(ICP), D1.H_C
  N11: U$1.PB4(MISO), D1.J_C
  N12: U$1.PB5(SCK), D1.I_C
  N13: U$1.PD2(INT0), D1.A_C
  N14: R1.Pin_1, D1.A_A, D1.B_A, D1.C_A, D1.D_A, D1.E_A, D1.F_A, D1.G_A, D1.H_A, D1.I_A, D1.J_A
